// Logisim project Additionneur1bitCin.circ as structural Verilog: 31 circuits, main circuit main
module main (
  input  [3:0] A,
  input  [3:0] B,
  input  [2:0] in_3,
  output out_4,
  output [3:0] out_5
);

  MultiplexerEntrer multiplexerentrer_1 (.A(B), .B(A), .Signal(in_3), .Out(out_5), .Overflow(out_4));
endmodule

module Addictionneur2Variables (
  input  in_1,
  input  in_2,
  output Res,
  output Cout
);

  xor xor_1 (Res, in_1, in_2);
  and and_1 (Cout, in_1, in_2);
endmodule

module Addictionneur3Variables (
  input  A,
  input  B,
  input  Cin,
  output Res,
  output Cout
);

  wire and_1_out, Cin___A___B_out, Cin___A_out, Cin___B_out, or_1_out, or_2_out, xor_1_out;

  xor xor_1 (xor_1_out, A, B);
  and and_1 (and_1_out, A, B);
  and Cin___B (Cin___B_out, Cin, B);
  and Cin___A (Cin___A_out, Cin, A);
  and Cin___A___B (Cin___A___B_out, A, Cin, B);
  xor xor_2 (Res, xor_1_out, Cin);
  or or_1 (or_1_out, and_1_out, Cin___B_out);
  or or_2 (or_2_out, Cin___A_out, Cin___A___B_out);
  or or_3 (Cout, or_1_out, or_2_out);

  // Notes on the sheet:
  //   A
  //   B
  //   CIN
  //   A & B
endmodule

// ADDITIONNEUR
module Additionneur4bits (
  input  [3:0] in_1,
  input  [3:0] in_2,
  output [4:0] out_3
);

  wire addictionneur2variables_1_cout, addictionneur3variables_2_cout, addictionneur3variables_3_cout;

  Addictionneur3Variables addictionneur3variables_1 (
    .A(in_1[3]), .B(in_2[3]), .Cin(addictionneur3variables_2_cout), .Res(out_3[3]), .Cout(out_3[4]));
  Addictionneur3Variables addictionneur3variables_2 (
    .A(in_1[2]), .B(in_2[2]), .Cin(addictionneur3variables_3_cout), .Res(out_3[2]),
    .Cout(addictionneur3variables_2_cout));
  Addictionneur3Variables addictionneur3variables_3 (
    .A(in_1[1]), .B(in_2[1]), .Cin(addictionneur2variables_1_cout), .Res(out_3[1]),
    .Cout(addictionneur3variables_3_cout));
  Addictionneur2Variables addictionneur2variables_1 (
    .in_1(in_1[0]), .in_2(in_2[0]), .Res(out_3[0]), .Cout(addictionneur2variables_1_cout));
endmodule

module TestAddition (
  input  in_1,
  input  in_2,
  output out_3
);

  wire or_1_out;

  not not_1 (out_3, or_1_out);
  or or_1 (or_1_out, in_1, in_2);
endmodule

module TestXor (
  input  in_1,
  input  in_2,
  output out_3
);

  wire not_1_out;

  not not_1 (not_1_out, in_1);
  and and_1 (out_3, not_1_out, in_2);
endmodule

module TestAnd (
  input  in_1,
  input  in_2,
  output out_3
);

  wire not_1_out;

  not not_1 (not_1_out, in_2);
  and and_1 (out_3, in_1, not_1_out);
endmodule

module TestOr (
  input  in_1,
  input  in_2,
  output out_3
);

  and and_1 (out_3, in_1, in_2);
endmodule

// AND
module And4bits (
  input  [3:0] in_1,
  input  [3:0] in_2,
  output [4:0] out_3
);

  wire not_1_out;

  and and_1 (out_3[3], in_1[3], in_2[3]);
  and and_2 (out_3[2], in_1[2], in_2[2]);
  and and_3 (out_3[1], in_1[1], in_2[1]);
  and and_4 (out_3[0], in_1[0], in_2[0]);
  not not_1 (not_1_out, out_3[3]);
  and and_5 (out_3[4], out_3[3], not_1_out);

  // Notes on the sheet:
  //   A
  //   B
endmodule

module TestTotal (
  input  in_1,
  input  in_2,
  output out_3,
  output out_4,
  output out_5,
  output out_6
);

  TestAddition testaddition_1 (.in_1(in_1), .in_2(in_2), .out_3(out_3));
  TestXor testxor_1 (.in_1(in_1), .in_2(in_2), .out_3(out_4));
  TestAnd testand_1 (.in_1(in_1), .in_2(in_2), .out_3(out_5));
  TestOr testor_1 (.in_1(in_1), .in_2(in_2), .out_3(out_6));
endmodule

module Execution (
  input  a4,
  input  a3,
  input  a2,
  input  a1,
  input  b4,
  input  b3,
  input  b2,
  input  b1,
  input  var2,
  input  var1,
  output V__Overflow,
  output N,
  output C,
  output res4,
  output res3,
  output res2,
  output res1
);

  wire additionneur4bits_1_p2, additionneur4bits_1_p4, additionneur4bits_1_p6, additionneur4bits_1_p8,
       additionneur4bits_1_p10, moduletest_1_p1, moduletest_1_p2, moduletest_1_p3, moduletest_1_p4,
       moduletest_1_p5, moduletest_1_p6, moduletest_1_p7, moduletest_1_p8, moduletest_1_p9, moduletest_1_p10,
       or4bits_1_p2, or4bits_1_p4, or4bits_1_p6, or4bits_1_p8, or4bits_1_p10, testtotal_1_out_3,
       testtotal_1_out_4, testtotal_1_out_5, testtotal_1_out_6;

  TestTotal testtotal_1 (
    .in_1(var1), .in_2(var2), .out_3(testtotal_1_out_3), .out_4(testtotal_1_out_4),
    .out_5(testtotal_1_out_5), .out_6(testtotal_1_out_6));
  // Additionneur4bits additionneur4bits_1: pin names not known; wires that end beside it: b2, additionneur4bits_1_p2, b1, additionneur4bits_1_p4, a4, additionneur4bits_1_p6, a3, additionneur4bits_1_p8, a2, additionneur4bits_1_p10, a1
  // Or4bits or4bits_1: pin names not known; wires that end beside it: b2, or4bits_1_p2, b1, or4bits_1_p4, a4, or4bits_1_p6, a3, or4bits_1_p8, a2, or4bits_1_p10, a1
  // ModuleTest moduletest_1: pin names not known; wires that end beside it: moduletest_1_p1, moduletest_1_p2, moduletest_1_p3, moduletest_1_p4, moduletest_1_p5, moduletest_1_p6, moduletest_1_p7, moduletest_1_p8, moduletest_1_p9, moduletest_1_p10, or4bits_1_p2, V__Overflow, or4bits_1_p4, res4, or4bits_1_p6, res3, or4bits_1_p8, res2, or4bits_1_p10, res1, additionneur4bits_1_p10, additionneur4bits_1_p8, additionneur4bits_1_p6, additionneur4bits_1_p4, additionneur4bits_1_p2, testtotal_1_out_4, testtotal_1_out_5, testtotal_1_out_6, testtotal_1_out_3
  // And4bits and4bits_1: pin names not known; wires that end beside it: b2, moduletest_1_p6, b1, moduletest_1_p7, a4, moduletest_1_p8, a3, moduletest_1_p9, a2, moduletest_1_p10, a1
  // Xor4bits xor4bits_1: pin names not known; wires that end beside it: b2, moduletest_1_p1, b1, moduletest_1_p2, a4, moduletest_1_p3, a3, moduletest_1_p4, a2, moduletest_1_p5, a1

  // Notes on the sheet:
  //   A
  //   B
endmodule

// OR
module Or4bits (
  input  [3:0] in_1,
  input  [3:0] in_2,
  output [4:0] out_3
);

  wire not_1_out;

  or or_1 (out_3[3], in_1[3], in_2[3]);
  or or_2 (out_3[2], in_1[2], in_2[2]);
  or or_3 (out_3[1], in_1[1], in_2[1]);
  or or_4 (out_3[0], in_1[0], in_2[0]);
  not not_1 (not_1_out, out_3[3]);
  and and_1 (out_3[4], out_3[3], not_1_out);

  // Notes on the sheet:
  //   A
  //   B
endmodule

// XOR
module Xor4bits (
  input  [3:0] in_1,
  input  [3:0] in_2,
  output [4:0] out_3
);

  wire not_1_out;

  xor xor_1 (out_3[3], in_1[3], in_2[3]);
  xor xor_2 (out_3[2], in_1[2], in_2[2]);
  xor xor_3 (out_3[1], in_1[1], in_2[1]);
  xor xor_4 (out_3[0], in_1[0], in_2[0]);
  not not_1 (not_1_out, out_3[3]);
  and and_1 (out_3[4], out_3[3], not_1_out);

  // Notes on the sheet:
  //   A
  //   B
endmodule

module Test (
  input  C,
  input  A,
  input  B,
  output Res
);

  wire and_1_out, and_2_out, and_3_out, and_4_out, not_1_out;

  not not_1 (not_1_out, C);
  and and_1 (and_1_out, C, A);
  and and_2 (and_2_out, not_1_out, B);
  and and_3 (and_3_out, A, A, and_1_out);
  and and_4 (and_4_out, and_2_out, B);
  or or_1 (Res, and_3_out, and_4_out);
endmodule

module Test4variables (
  input  C,
  input  A,
  input  B,
  input  in_4,
  input  in_5,
  input  A_2,
  input  B_2,
  input  C_2,
  input  D,
  output Res,
  output Res_2
);

  wire and_1_out, and_2_out, and_3_out, and_4_out, and_5_out, and_6_out, and_7_out, and_8_out, and_9_out,
       and_10_out, and_11_out, and_12_out, not_1_out, testtotal_1_out_3, testtotal_1_out_4,
       testtotal_1_out_5, testtotal_1_out_6;

  TestTotal testtotal_1 (
    .in_1(in_5), .in_2(in_4), .out_3(testtotal_1_out_3), .out_4(testtotal_1_out_4),
    .out_5(testtotal_1_out_5), .out_6(testtotal_1_out_6));
  not not_1 (not_1_out, C);
  and and_1 (and_1_out, testtotal_1_out_3, A_2);
  and and_2 (and_2_out, testtotal_1_out_4, B_2);
  and and_3 (and_3_out, testtotal_1_out_5, C_2);
  and and_4 (and_4_out, testtotal_1_out_6, D);
  and and_5 (and_5_out, C, A);
  and and_6 (and_6_out, not_1_out, B);
  and and_7 (and_7_out, A_2, and_1_out);
  and and_8 (and_8_out, B_2, and_2_out);
  and and_9 (and_9_out, C_2, and_3_out);
  and and_10 (and_10_out, D, and_4_out);
  and and_11 (and_11_out, A, A, and_5_out);
  and and_12 (and_12_out, and_6_out, B);
  or or_1 (Res, and_11_out, and_12_out);
  or or_2 (Res_2, and_7_out, and_8_out, and_9_out, and_10_out);
endmodule

module ModuleTest (
  input  ADD,
  input  OR,
  input  AND,
  input  XOR,
  input  ADD1,
  input  ADD2,
  input  ADD3,
  input  ADD4,
  input  ADDV,
  input  OR1,
  input  OR2,
  input  OR3,
  input  OR4,
  input  ORV,
  input  AND1,
  input  AND2,
  input  AND3,
  input  AND4,
  input  ANDV,
  input  XOR1,
  input  XOR2,
  input  XOR3,
  input  XOR4,
  input  XORV,
  output res1,
  output res2,
  output res3,
  output res4,
  output resV
);

  wire and_1_out, and_2_out, and_3_out, and_4_out, and_5_out, and_6_out, and_7_out, and_8_out, and_9_out,
       and_10_out, and_11_out, and_12_out, and_13_out, and_14_out, and_15_out, and_16_out, and_17_out,
       and_18_out, and_19_out, and_20_out, and_21_out, and_22_out, and_23_out, and_24_out, and_25_out,
       and_26_out, and_27_out, and_28_out, and_29_out, and_30_out, and_31_out, and_32_out, and_33_out,
       and_34_out, and_35_out, and_36_out, and_37_out, and_38_out, and_39_out, and_40_out;

  and and_1 (and_1_out, ADD, ADD1);
  and and_2 (and_2_out, ADD, ADD2);
  and and_3 (and_3_out, ADD3, ADD);
  and and_4 (and_4_out, ADD4, ADD);
  and and_5 (and_5_out, ADD, ADDV);
  and and_6 (and_6_out, OR, OR1);
  and and_7 (and_7_out, OR, OR2);
  and and_8 (and_8_out, OR3, OR);
  and and_9 (and_9_out, OR4, OR);
  and and_10 (and_10_out, OR, ORV);
  and and_11 (and_11_out, AND, AND1);
  and and_12 (and_12_out, AND, AND2);
  and and_13 (and_13_out, AND3, AND);
  and and_14 (and_14_out, AND4, AND);
  and and_15 (and_15_out, AND, ANDV);
  and and_16 (and_16_out, XOR, XOR1);
  and and_17 (and_17_out, XOR, XOR2);
  and and_18 (and_18_out, XOR3, XOR);
  and and_19 (and_19_out, XOR4, XOR);
  and and_20 (and_20_out, XORV, XOR);
  and and_21 (and_21_out, ADD2, ADD2, and_2_out);
  and and_22 (and_22_out, ADD1, and_1_out);
  and and_23 (and_23_out, ADD3, ADD3, and_3_out);
  and and_24 (and_24_out, and_4_out, ADD4);
  and and_25 (and_25_out, ADDV, and_5_out);
  and and_26 (and_26_out, OR1, and_6_out);
  and and_27 (and_27_out, OR2, and_7_out);
  and and_28 (and_28_out, OR3, OR3, and_8_out);
  and and_29 (and_29_out, and_9_out, OR4);
  and and_30 (and_30_out, ORV, and_10_out);
  and and_31 (and_31_out, AND1, and_11_out);
  and and_32 (and_32_out, AND2, and_12_out);
  and and_33 (and_33_out, AND3, AND3, and_13_out);
  and and_34 (and_34_out, and_14_out, AND4);
  and and_35 (and_35_out, ANDV, and_15_out);
  and and_36 (and_36_out, XOR1, and_16_out);
  and and_37 (and_37_out, XOR2, and_17_out);
  and and_38 (and_38_out, XOR3, XOR3, and_18_out);
  and and_39 (and_39_out, and_19_out, XOR4);
  and and_40 (and_40_out, XORV, and_20_out);
  or or_1 (res1, and_22_out, and_31_out, and_26_out, and_36_out);
  or or_2 (res2, and_21_out, and_27_out, and_32_out, and_37_out);
  or or_3 (res3, and_23_out, and_33_out, and_28_out, and_38_out);
  or or_4 (res4, and_39_out, and_34_out, and_24_out, and_29_out);
  or or_5 (resV, and_25_out, and_35_out, and_30_out, and_40_out);
endmodule

module Registre4bits (
  input  [3:0] In,
  input  Clock,
  output [3:0] Out
);

  D_Flip_Flop d_ff_1 (.clk(Clock), .D(In[0]), .Q(Out[0]));  // open: Qn, preset, en, reset
  D_Flip_Flop d_ff_2 (.clk(Clock), .D(In[1]), .Q(Out[1]));  // open: Qn, preset, en, reset
  D_Flip_Flop d_ff_3 (.clk(Clock), .D(In[2]), .Q(Out[2]));  // open: Qn, preset, en, reset
  D_Flip_Flop d_ff_4 (.clk(Clock), .D(In[3]), .Q(Out[3]));  // open: Qn, preset, en, reset
endmodule

module MultiplexerEntrer (
  input  [3:0] A,
  input  [3:0] B,
  input  [2:0] Signal,
  output [3:0] Out,
  output Overflow
);

  wire [3:0] demultiplexer_1_out2, demultiplexer_1_out3, demultiplexer_1_out4, demultiplexer_1_out5,
       demultiplexer_2_out2, demultiplexer_2_out3, demultiplexer_2_out4, demultiplexer_2_out5;
  wire [4:0] additionneur4bits_1_out_3, and4bits_1_out_3, or4bits_1_out_3, undriven, xor4bits_1_out_3;

  Demultiplexer #(.select(3), .width(4), .enable("false")) demultiplexer_1 (
    .out2(demultiplexer_1_out2), .out3(demultiplexer_1_out3), .out4(demultiplexer_1_out4),
    .out5(demultiplexer_1_out5), .in(A), .sel(Signal));  // open: out0, out1, out6, out7
  Demultiplexer #(.select(3), .width(4), .enable("false")) demultiplexer_2 (
    .out2(demultiplexer_2_out2), .out3(demultiplexer_2_out3), .out4(demultiplexer_2_out4),
    .out5(demultiplexer_2_out5), .in(B), .sel(Signal));  // open: out0, out1, out6, out7
  Additionneur4bits additionneur4bits_1 (
    .in_1(demultiplexer_1_out2), .in_2(demultiplexer_2_out2), .out_3(additionneur4bits_1_out_3));
  And4bits and4bits_1 (.in_1(demultiplexer_1_out3), .in_2(demultiplexer_2_out3), .out_3(and4bits_1_out_3));
  Or4bits or4bits_1 (.in_1(demultiplexer_1_out4), .in_2(demultiplexer_2_out4), .out_3(or4bits_1_out_3));
  Xor4bits xor4bits_1 (.in_1(demultiplexer_1_out5), .in_2(demultiplexer_2_out5), .out_3(xor4bits_1_out_3));
  Multiplexer #(.select(3), .width(5), .enable("false")) multiplexer_1 (
    .in0(undriven), .in2(additionneur4bits_1_out_3), .in3(and4bits_1_out_3), .in4(or4bits_1_out_3),
    .in5(xor4bits_1_out_3), .in6(5'b00001), .out({Overflow, Out}), .sel(Signal));  // open: in1, in7

  // Notes on the sheet:
  //   100 OR
  //   010 ADD
  //   011 AND
  //   101 XOR
  //   110 Init
endmodule

module UAL (
  input  [3:0] A,
  input  [3:0] B,
  input  [2:0] OP,
  output out_4,
  output [3:0] Out
);

  MultiplexerEntrer multiplexerentrer_1 (.A(B), .B(A), .Signal(OP), .Out(Out), .Overflow(out_4));

  // Notes on the sheet:
  //   100 OR
  //   010 ADD
  //   011 AND
  //   101 XOR
  //   110 Init
endmodule

module Additionneur8Bits (
  input  in_1,
  input  [7:0] in_2,
  output [7:0] out_3
);

  wire addictionneur2variables_1_cout, addictionneur3variables_2_cout, addictionneur3variables_3_cout,
       addictionneur3variables_4_cout, addictionneur3variables_5_cout, addictionneur3variables_6_cout,
       addictionneur3variables_7_cout;

  Addictionneur3Variables addictionneur3variables_1 (
    .A(1'b0), .B(in_2[7]), .Cin(addictionneur3variables_2_cout), .Res(out_3[7]));  // open: Cout
  Addictionneur3Variables addictionneur3variables_2 (
    .A(in_2[6]), .B(1'b0), .Cin(addictionneur3variables_3_cout), .Res(out_3[6]),
    .Cout(addictionneur3variables_2_cout));
  Addictionneur3Variables addictionneur3variables_3 (
    .A(1'b0), .B(in_2[5]), .Cin(addictionneur3variables_4_cout), .Res(out_3[5]),
    .Cout(addictionneur3variables_3_cout));
  Addictionneur3Variables addictionneur3variables_4 (
    .A(in_2[4]), .B(1'b0), .Cin(addictionneur3variables_5_cout), .Res(out_3[4]),
    .Cout(addictionneur3variables_4_cout));
  Addictionneur3Variables addictionneur3variables_5 (
    .A(in_2[3]), .B(1'b0), .Cin(addictionneur3variables_6_cout), .Res(out_3[3]),
    .Cout(addictionneur3variables_5_cout));
  Addictionneur3Variables addictionneur3variables_6 (
    .A(1'b0), .B(in_2[2]), .Cin(addictionneur3variables_7_cout), .Res(out_3[2]),
    .Cout(addictionneur3variables_6_cout));
  Addictionneur3Variables addictionneur3variables_7 (
    .A(1'b0), .B(in_2[1]), .Cin(addictionneur2variables_1_cout), .Res(out_3[1]),
    .Cout(addictionneur3variables_7_cout));
  Addictionneur2Variables addictionneur2variables_1 (
    .in_1(in_1), .in_2(in_2[0]), .Res(out_3[0]), .Cout(addictionneur2variables_1_cout));
endmodule

module Compteur8Bits (
  input  Clock,
  input  Start,
  output [7:0] Instructions
);

  wire and_2_out, and_3_out, multiplexer_2_out, not_1_out, or_1_out;
  wire [7:0] Additionneur_out_3, and_1_out, multiplexer_1_out;

  or or_1 (or_1_out, Clock, and_3_out);
  Additionneur8Bits Additionneur (.in_1(Clock), .in_2(Instructions), .out_3(Additionneur_out_3));
  Multiplexer #(.width(8), .enable("false")) multiplexer_1 (
    .in0(Additionneur_out_3), .in1({8{1'b0}}), .out(multiplexer_1_out), .sel(Start));
  not not_1 (not_1_out, or_1_out);
  Multiplexer #(.enable("false")) multiplexer_2 (.in0(not_1_out), .in1(Clock), .out(multiplexer_2_out), .sel(Start));
  Registre8Bits registre8bits_1 (.In(multiplexer_1_out), .Clock(multiplexer_2_out), .Out(Instructions));
  assign and_1_out = {8{1'b1}} & Instructions;  // AND_Gate and_1, 8 bits wide
  and and_2 (and_2_out, and_1_out[7], and_1_out[6], and_1_out[5], and_1_out[4], and_1_out[3]);
  and and_3 (and_3_out, and_2_out, and_1_out[2], and_1_out[1], and_1_out[0]);
endmodule

module ProcesseurSansRAM (
  input  Start,
  output [7:0] out_2
);

  wire clock_1_out;
  wire [1:0] decodeursansram_1_a, decodeursansram_1_b, decodeursansram_1_registre;
  wire [2:0] decodeursansram_1_op;
  wire [8:0] ram_1_data;

  Clock clock_1 (.out(clock_1_out));
  RAM #(.dataWidth(9)) ram_1 (.addr(out_2), .data(ram_1_data));  // open: sel, clk, ld, clr
  Compteur8Bits Compteur (.Clock(clock_1_out), .Start(Start), .Instructions(out_2));
  DecodeurSansRam decodeursansram_1 (
    .in_1(ram_1_data), .OP(decodeursansram_1_op), .B(decodeursansram_1_b), .A(decodeursansram_1_a),
    .Registre(decodeursansram_1_registre));
  UniteCommandeSansRAM Unite_de_commande (
    .Clock(clock_1_out), .Registre(decodeursansram_1_registre), .A(decodeursansram_1_a),
    .B(decodeursansram_1_b), .OP(decodeursansram_1_op));

  // Notes on the sheet:
  //   100 OR
  //   010 ADD
  //   011 AND
  //   101 XOR
  //   110 Init
  //   Jeux d'instructions
  //   2 b => Registre / 2 b => A / 2 b =>B / 3 b => OP 
endmodule

module Registre (
  input  [3:0] Value,
  input  Clock,
  input  [1:0] SignalRegistre,
  output [3:0] out_4,
  output [3:0] out_5,
  output [3:0] out_6,
  output [3:0] out_7
);

  wire demultiplexer_1_out0, demultiplexer_1_out1, demultiplexer_1_out2, demultiplexer_1_out3;
  wire [3:0] demultiplexer_2_out0, demultiplexer_2_out1, demultiplexer_2_out2, demultiplexer_2_out3;

  Demultiplexer #(.select(2), .enable("false")) demultiplexer_1 (
    .out0(demultiplexer_1_out0), .out1(demultiplexer_1_out1), .out2(demultiplexer_1_out2),
    .out3(demultiplexer_1_out3), .in(Clock), .sel(SignalRegistre));
  Demultiplexer #(.select(2), .width(4), .enable("false")) demultiplexer_2 (
    .out0(demultiplexer_2_out0), .out1(demultiplexer_2_out1), .out2(demultiplexer_2_out2),
    .out3(demultiplexer_2_out3), .in(Value), .sel(SignalRegistre));
  Registre4bits registre4bits_1 (.In(demultiplexer_2_out0), .Clock(demultiplexer_1_out0), .Out(out_4));
  Registre4bits registre4bits_2 (.In(demultiplexer_2_out1), .Clock(demultiplexer_1_out1), .Out(out_5));
  Registre4bits registre4bits_3 (.In(demultiplexer_2_out2), .Clock(demultiplexer_1_out2), .Out(out_6));
  Registre4bits registre4bits_4 (.In(demultiplexer_2_out3), .Clock(demultiplexer_1_out3), .Out(out_7));
endmodule

module Registre8Bits (
  input  [7:0] In,
  input  Clock,
  output [7:0] Out
);

  Registre4bits registre4bits_1 (.In(In[3:0]), .Clock(Clock), .Out(Out[3:0]));
  Registre4bits registre4bits_2 (.In(In[7:4]), .Clock(Clock), .Out(Out[7:4]));
endmodule

module UniteCommandeSansRAM (
  input  Clock,
  input  [1:0] Registre,
  input  [1:0] A,
  input  [1:0] B,
  input  [2:0] OP
);

  wire [3:0] AccesRegistre_2_out, AccesRegistre_out, Registre_out_4, Registre_out_5, Registre_out_6,
       Registre_out_7, UAL_out;

  Registre u_Registre (
    .Value(UAL_out), .Clock(Clock), .SignalRegistre(Registre), .out_4(Registre_out_4),
    .out_5(Registre_out_5), .out_6(Registre_out_6), .out_7(Registre_out_7));
  AccesRegistre AccesRegistre (
    ._11(Registre_out_7), ._00(Registre_out_4), ._01(Registre_out_5), ._10(Registre_out_6), .Signal(A),
    .Out(AccesRegistre_out));
  AccesRegistre AccesRegistre_2 (
    ._11(Registre_out_7), ._00(Registre_out_4), ._01(Registre_out_5), ._10(Registre_out_6), .Signal(B),
    .Out(AccesRegistre_2_out));
  UAL UAL (.OP(OP), .A(AccesRegistre_out), .B(AccesRegistre_2_out), .Out(UAL_out));  // open: out_4

  // Notes on the sheet:
  //   100 OR
  //   010 ADD
  //   011 AND
  //   101 XOR
  //   110 Init
endmodule

module AccesRegistre (
  input  [3:0] _11,
  input  [3:0] _00,
  input  [3:0] _01,
  input  [3:0] _10,
  input  [1:0] Signal,
  output [3:0] Out
);

  Multiplexer #(.select(2), .width(4), .enable("false")) multiplexer_1 (
    .in0(_00), .in1(_01), .in2(_10), .in3(_11), .out(Out), .sel(Signal));
endmodule

// Decodeur
module DecodeurSansRam (
  input  [8:0] in_1,
  output [2:0] OP,
  output [1:0] B,
  output [1:0] A,
  output [1:0] Registre
);

  wire or_1_out, or_2_out;

  Demultiplexer #(.width(9), .enable("false")) demultiplexer_1 (
    .out1({Registre, A, B, OP}), .in(in_1), .sel(or_2_out));  // open: out0
  or or_1 (or_1_out, in_1[8], in_1[7], in_1[6], in_1[5], in_1[4]);
  or or_2 (or_2_out, in_1[3], in_1[2], in_1[1], in_1[0], or_1_out);
endmodule

module Processeur (
  input  Start,
  input  [7:0] in_2,
  input  [11:0] in_3,
  input  in_4,
  input  in_5,
  output [7:0] out_6
);

  wire Clock, Str;
  wire [1:0] decodeur_1_signal;
  wire [3:0] ValueIn, ValueOut;
  wire [7:0] Adress;
  wire [9:0] decodeur_1_data;
  wire [11:0] ram_1_data;

  RAM #(.dataWidth(12)) ram_1 (.addr(out_6), .data(ram_1_data));  // open: sel, clk, ld, clr
  Clock clock_1 (.out(Clock));
  Compteur8Bits Compteur (.Clock(Clock), .Start(Start), .Instructions(out_6));
  Decodeur decodeur_1 (.in_1(ram_1_data), .Signal(decodeur_1_signal), .Data(decodeur_1_data));
  UniteCommande unitecommande_1 (
    .Clock(Clock), .Data(decodeur_1_data), .Signal(decodeur_1_signal), .Str(Str), .ValueRam(ValueOut),
    .Adress(Adress), .ValueToStock(ValueIn));
  RAM #(.dataWidth(4), .bus("separate")) ram_2 (
    .addr(Adress), .din(ValueIn), .data(ValueOut), .str(Str), .clk(Clock));  // open: sel, ld, clr
  RAM #(.dataWidth(12), .bus("separate")) ram_3 (
    .addr(in_2), .din(in_3), .str(in_4), .clk(in_5));  // open: data, sel, ld, clr

  // Notes on the sheet:
  //   Jeux d'instructions
  //   110000000110 Initialisation de 0001 dans le registre 00 => c06
  //   100000000100 Mise en mémoire du registre 00 dans la case 00000001 => 804
  //   010000000111 La case 00000001 de la mémoire est mise dans le registre 11 => 407
  //   110100011010 Addition de la case 00 et 11 résultat mis dans la case 10 => d1a
  //   100000001010 Mise en mémoire du registre 10 dans la case 00000010 => 822
  //   100 OR
  //   010 ADD
  //   011 AND
  //   101 XOR
  //   110 Init
  //   01 Load ( M to R )    8 b => Adress / 2 b => registre
  //   10 Store ( R to M )   8 b => Adress / 2 b => regitre
  //   2 b =>  choix / 10 b => Infos     ====> 12 b
  //   11  OP      1 b => Inutile / 2 b => Registre / 2 b => A / 2 b =>B / 3 b => OP 
endmodule

module UniteCommande (
  input  Clock,
  input  [3:0] ValueRam,
  input  [9:0] Data,
  input  [1:0] Signal,
  output Str,
  output [7:0] Adress,
  output [3:0] ValueToStock
);

  wire and_1_out, ClockDirection, demultiplexer_2_out1, load_store_1_registerdirectionlocation,
       RegisterDirectionValue;
  wire [1:0] A, B, multiplexer_2_out, Registre, RegistreL_S;
  wire [2:0] OP;
  wire [3:0] AccesRegistre_2_out, AccesRegistre_out, multiplexer_1_out, Registre_out_4, Registre_out_5,
       Registre_out_6, Registre_out_7, UAL_out;
  wire [9:0] Load_Store;
  wire [9:9] demultiplexer_1_out1;

  Load_Store load_store_1 (
    .Adress(Load_Store), .Signal(Signal), .Registre(RegistreL_S), .Adress_2(Adress), .Str(Str),
    .ClockDirection(ClockDirection), .RegisteDirectionValue(RegisterDirectionValue),
    .RegisterDirectionLocation(load_store_1_registerdirectionlocation));
  Demultiplexer #(.width(10), .enable("false")) demultiplexer_1 (
    .out0(Load_Store), .out1({demultiplexer_1_out1[9], Registre, A, B, OP}), .in(Data), .sel(and_1_out));
  and and_1 (and_1_out, Signal[0], Signal[1]);
  Multiplexer #(.width(4), .enable("false")) multiplexer_1 (
    .in0(UAL_out), .in1(ValueRam), .out(multiplexer_1_out), .sel(RegisterDirectionValue));
  Multiplexer #(.width(2), .enable("false")) multiplexer_2 (
    .in0(Registre), .in1(RegistreL_S), .out(multiplexer_2_out), .sel(load_store_1_registerdirectionlocation));
  Demultiplexer #(.enable("false")) demultiplexer_2 (
    .out1(demultiplexer_2_out1), .in(Clock), .sel(ClockDirection));  // open: out0
  AccesRegistre AccesRegistre (
    ._11(Registre_out_7), ._00(Registre_out_4), ._01(Registre_out_5), ._10(Registre_out_6), .Signal(A),
    .Out(AccesRegistre_out));
  AccesRegistre AccesRegistre_2 (
    ._11(Registre_out_7), ._00(Registre_out_4), ._01(Registre_out_5), ._10(Registre_out_6), .Signal(B),
    .Out(AccesRegistre_2_out));
  UAL UAL (.OP(OP), .A(AccesRegistre_out), .B(AccesRegistre_2_out), .Out(UAL_out));  // open: out_4
  Registre u_Registre (
    .Value(multiplexer_1_out), .Clock(demultiplexer_2_out1), .SignalRegistre(multiplexer_2_out),
    .out_4(Registre_out_4), .out_5(Registre_out_5), .out_6(Registre_out_6), .out_7(Registre_out_7));
  AccesRegistre AccesRegistre_3 (
    ._11(Registre_out_7), ._00(Registre_out_4), ._01(Registre_out_5), ._10(Registre_out_6),
    .Signal(RegistreL_S), .Out(ValueToStock));

  // Notes on the sheet:
  //   110 Init
  //   100 OR
  //   010 ADD
  //   011 AND
  //   101 XOR
  //   110000000110 Initialisation de 0001 dans le registre 00 => c06
  //   100000000100 Mise en mémoire du registre 00 dans la case 00000001 => 804
  //   10000000100010 Mise en mémoire du registre 10 dans la case 00000010 => 822
  //   01 Load ( M to R )    8 b => Adress / 2 b => registre
  //   10 Store ( R to M )   8 b => Adress / 2 b => regitre
  //   2 b =>  choix / 10 b => Infos     ====> 12 b
  //   010000000111 La case 00000001 de la mémoire est mise dans le registre 11 => 407
  //   110100011010 Addition de la case 00 et 11 résultat mis dans la case 10 => d1a
  //   Envoi la donnée dans l'UAL ou dans le Load / Store
  //   11  OP      1 b => Inutile / 2 b => Registre / 2 b => A / 2 b =>B / 3 b => OP 
endmodule

module Load_Store (
  input  [9:0] Adress,
  input  [1:0] Signal,
  output [1:0] Registre,
  output [7:0] Adress_2,
  output Str,
  output ClockDirection,
  output RegisteDirectionValue,
  output RegisterDirectionLocation
);

  wire and_1_out, and_2_out, and_4_out, not_1_out, not_2_out;

  not not_1 (not_1_out, Signal[1]);
  and and_1 (and_1_out, not_1_out, Signal[0]);
  and and_2 (and_2_out, Signal[0], Signal[1]);
  not not_2 (not_2_out, Signal[1]);
  not not_3 (Str, Signal[0]);
  or or_1 (ClockDirection, and_1_out, and_2_out);
  and and_3 (RegisteDirectionValue, Signal[0], not_2_out);
  not not_4 (RegisterDirectionLocation, and_4_out);
  and and_4 (and_4_out, Signal[0], Signal[1]);

  assign Adress_2 = Adress[9:2];
  assign Registre = Adress[1:0];

  // Notes on the sheet:
  //   11 OP
  //   01 Load ( M to R )    8 b => Adress / 2 b => registre
  //   10 Store ( R to M )   8 b => Adress / 2 b => regitre
  //   2 b =>  choix / 10 b => Infos     ====> 12 b
  //   11  OP      1 b => Inutile / 2 b => Registre / 2 b => A / 2 b =>B / 3 b => OP 
endmodule

module Decodeur (
  input  [11:0] in_1,
  output [1:0] Signal,
  output [9:0] Data
);

  wire or_1_out, or_2_out, or_3_out;

  Demultiplexer #(.width(12), .enable("false")) demultiplexer_1 (
    .out1({Signal, Data}), .in(in_1), .sel(or_3_out));  // open: out0
  or or_1 (or_1_out, in_1[11], in_1[10], in_1[9], in_1[8], in_1[7]);
  or or_2 (or_2_out, in_1[6], in_1[5], in_1[4], in_1[3], or_1_out);
  or or_3 (or_3_out, in_1[2], in_1[1], in_1[0]);
endmodule
